# Fritzing sketch rfm69w-breakout (saved by Fritzing 0.9.3b)
circuit board: 8.9cm x 9.12cm
breadboards: 1
stripboards: 1

parts:
  Part1 = RFM69W
  J1 = female pin header, 8 pins [form="♀ (female)"]
  J2 = female pin header, 8 pins [form="♀ (female)"]
  J3 = female pin header, 8 pins [form="♀ (female)"]
  J4 = female pin header, 8 pins [form="♀ (female)"]
  Part2 = RFM69W
  J5 = female pin header, 8 pins [form="♀ (female)"]
  J6 = female pin header, 8 pins [form="♀ (female)"]
  J7 = female pin header, 8 pins [form="♀ (female)"]
  J8 = female pin header, 8 pins [form="♀ (female)"]
  Part3 = RFM69W
  Part4 = RFM69W
  J9 = female pin header, 8 pins [form="♀ (female)"]
  J10 = female pin header, 8 pins [form="♀ (female)"]
  J11 = female pin header, 8 pins [form="♀ (female)"]
  J12 = female pin header, 8 pins [form="♀ (female)"]
  Part5 = RFM69W
  Part6 = RFM69W
  J13 = female pin header, 8 pins [form="♀ (female)"]
  J14 = female pin header, 8 pins [form="♀ (female)"]
  J15 = female pin header, 8 pins [form="♀ (female)"]
  J16 = female pin header, 8 pins [form="♀ (female)"]
  Part7 = RFM69W
  Part8 = RFM69W
  J17 = female pin header, 8 pins [form="♀ (female)"]
  J19 = female pin header, 8 pins [form="♀ (female)"]
  Part9 = RFM69W
  J20 = female pin header, 8 pins [form="♀ (female)"]
  J21 = female pin header, 8 pins [form="♀ (female)"]
  Part10 = RFM69W
  J22 = female pin header, 8 pins [form="♀ (female)"]
  J23 = female pin header, 8 pins [form="♀ (female)"]
  Part11 = RFM69W
  J24 = female pin header, 8 pins [form="♀ (female)"]
  J25 = female pin header, 8 pins [form="♀ (female)"]
  Part12 = RFM69W

nets:
  N1: Part1.RESET, J1.pin1
  N2: Part1.DIO0, J1.pin2
  N3: Part1.DIO1, J1.pin3
  N4: Part1.DIO2, J1.pin4
  N5: Part1.DIO3, J1.pin5
  N6: Part1.DIO4, J1.pin6
  N7: Part1.DIO5, J1.pin7
  N8: Part1.3V3, J1.pin8
  N9: Part1.GND#8, J2.pin8
  N10: Part1.ANA, J2.pin7
  N11: Part1.GND#10, J2.pin6
  N12: Part1.SCK, J2.pin5
  N13: Part1.MISO, J2.pin4
  N14: Part1.MOSI, J2.pin3
  N15: Part1.NSS, J2.pin2
  N16: Part1.NC, J2.pin1
  N17: J3.pin1, Part2.RESET
  N18: J3.pin2, Part2.DIO0
  N19: J3.pin3, Part2.DIO1
  N20: J3.pin4, Part2.DIO2
  N21: J3.pin5, Part2.DIO3
  N22: J3.pin6, Part2.DIO4
  N23: J3.pin7, Part2.DIO5
  N24: J3.pin8, Part2.3V3
  N25: J4.pin1, Part2.NC
  N26: J4.pin2, Part2.NSS
  N27: J4.pin3, Part2.MOSI
  N28: J4.pin4, Part2.MISO
  N29: J4.pin5, Part2.SCK
  N30: J4.pin6, Part2.GND#10
  N31: J4.pin7, Part2.ANA
  N32: J4.pin8, Part2.GND#8
  N33: J5.pin1, Part3.NC
  N34: J5.pin2, Part3.NSS
  N35: J5.pin3, Part3.MOSI
  N36: J5.pin4, Part3.MISO
  N37: J5.pin5, Part3.SCK
  N38: J5.pin6, Part3.GND#10
  N39: J5.pin7, Part3.ANA
  N40: J5.pin8, Part3.GND#8
  N41: J6.pin1, Part4.NC
  N42: J6.pin2, Part4.NSS
  N43: J6.pin3, Part4.MOSI
  N44: J6.pin4, Part4.MISO
  N45: J6.pin5, Part4.SCK
  N46: J6.pin6, Part4.GND#10
  N47: J6.pin7, Part4.ANA
  N48: J6.pin8, Part4.GND#8
  N49: J7.pin1, Part3.RESET
  N50: J7.pin2, Part3.DIO0
  N51: J7.pin3, Part3.DIO1
  N52: J7.pin4, Part3.DIO2
  N53: J7.pin5, Part3.DIO3
  N54: J7.pin6, Part3.DIO4
  N55: J7.pin7, Part3.DIO5
  N56: J7.pin8, Part3.3V3
  N57: J8.pin1, Part4.RESET
  N58: J8.pin2, Part4.DIO0
  N59: J8.pin3, Part4.DIO1
  N60: J8.pin4, Part4.DIO2
  N61: J8.pin5, Part4.DIO3
  N62: J8.pin6, Part4.DIO4
  N63: J8.pin7, Part4.DIO5
  N64: J8.pin8, Part4.3V3
  N65: J9.pin1, Part5.NC
  N66: J9.pin2, Part5.NSS
  N67: J9.pin3, Part5.MOSI
  N68: J9.pin4, Part5.MISO
  N69: J9.pin5, Part5.SCK
  N70: J9.pin6, Part5.GND#10
  N71: J9.pin7, Part5.ANA
  N72: J9.pin8, Part5.GND#8
  N73: J10.pin1, Part6.NC
  N74: J10.pin2, Part6.NSS
  N75: J10.pin3, Part6.MOSI
  N76: J10.pin4, Part6.MISO
  N77: J10.pin5, Part6.SCK
  N78: J10.pin6, Part6.GND#10
  N79: J10.pin7, Part6.ANA
  N80: J10.pin8, Part6.GND#8
  N81: J11.pin1, Part5.RESET
  N82: J11.pin2, Part5.DIO0
  N83: J11.pin3, Part5.DIO1
  N84: J11.pin4, Part5.DIO2
  N85: J11.pin5, Part5.DIO3
  N86: J11.pin6, Part5.DIO4
  N87: J11.pin7, Part5.DIO5
  N88: J11.pin8, Part5.3V3
  N89: J12.pin1, Part6.RESET
  N90: J12.pin2, Part6.DIO0
  N91: J12.pin3, Part6.DIO1
  N92: J12.pin4, Part6.DIO2
  N93: J12.pin5, Part6.DIO3
  N94: J12.pin6, Part6.DIO4
  N95: J12.pin7, Part6.DIO5
  N96: J12.pin8, Part6.3V3
  N97: J13.pin1, Part7.NC
  N98: J13.pin2, Part7.NSS
  N99: J13.pin3, Part7.MOSI
  N100: J13.pin4, Part7.MISO
  N101: J13.pin5, Part7.SCK
  N102: J13.pin6, Part7.GND#10
  N103: J13.pin7, Part7.ANA
  N104: J13.pin8, Part7.GND#8
  N105: J14.pin1, Part8.NC
  N106: J14.pin2, Part8.NSS
  N107: J14.pin3, Part8.MOSI
  N108: J14.pin4, Part8.MISO
  N109: J14.pin5, Part8.SCK
  N110: J14.pin6, Part8.GND#10
  N111: J14.pin7, Part8.ANA
  N112: J14.pin8, Part8.GND#8
  N113: J15.pin1, Part7.RESET
  N114: J15.pin2, Part7.DIO0
  N115: J15.pin3, Part7.DIO1
  N116: J15.pin4, Part7.DIO2
  N117: J15.pin5, Part7.DIO3
  N118: J15.pin6, Part7.DIO4
  N119: J15.pin7, Part7.DIO5
  N120: J15.pin8, Part7.3V3
  N121: J16.pin1, Part8.RESET
  N122: J16.pin2, Part8.DIO0
  N123: J16.pin3, Part8.DIO1
  N124: J16.pin4, Part8.DIO2
  N125: J16.pin5, Part8.DIO3
  N126: J16.pin6, Part8.DIO4
  N127: J16.pin7, Part8.DIO5
  N128: J16.pin8, Part8.3V3
  N129: J17.pin1, Part9.NC
  N130: J17.pin2, Part9.NSS
  N131: J17.pin3, Part9.MOSI
  N132: J17.pin4, Part9.MISO
  N133: J17.pin5, Part9.SCK
  N134: J17.pin6, Part9.GND#10
  N135: J17.pin7, Part9.ANA
  N136: J17.pin8, Part9.GND#8
  N137: J19.pin1, Part9.RESET
  N138: J19.pin2, Part9.DIO0
  N139: J19.pin3, Part9.DIO1
  N140: J19.pin4, Part9.DIO2
  N141: J19.pin5, Part9.DIO3
  N142: J19.pin6, Part9.DIO4
  N143: J19.pin7, Part9.DIO5
  N144: J19.pin8, Part9.3V3
  N145: J20.pin1, Part10.NC
  N146: J20.pin2, Part10.NSS
  N147: J20.pin3, Part10.MOSI
  N148: J20.pin4, Part10.MISO
  N149: J20.pin5, Part10.SCK
  N150: J20.pin6, Part10.GND#10
  N151: J20.pin7, Part10.ANA
  N152: J20.pin8, Part10.GND#8
  N153: J21.pin1, Part10.RESET
  N154: J21.pin2, Part10.DIO0
  N155: J21.pin3, Part10.DIO1
  N156: J21.pin4, Part10.DIO2
  N157: J21.pin5, Part10.DIO3
  N158: J21.pin6, Part10.DIO4
  N159: J21.pin7, Part10.DIO5
  N160: J21.pin8, Part10.3V3
  N161: J22.pin1, Part11.NC
  N162: J22.pin2, Part11.NSS
  N163: J22.pin3, Part11.MOSI
  N164: J22.pin4, Part11.MISO
  N165: J22.pin5, Part11.SCK
  N166: J22.pin6, Part11.GND#10
  N167: J22.pin7, Part11.ANA
  N168: J22.pin8, Part11.GND#8
  N169: J23.pin1, Part11.RESET
  N170: J23.pin2, Part11.DIO0
  N171: J23.pin3, Part11.DIO1
  N172: J23.pin4, Part11.DIO2
  N173: J23.pin5, Part11.DIO3
  N174: J23.pin6, Part11.DIO4
  N175: J23.pin7, Part11.DIO5
  N176: J23.pin8, Part11.3V3
  N177: J24.pin1, Part12.NC
  N178: J24.pin2, Part12.NSS
  N179: J24.pin3, Part12.MOSI
  N180: J24.pin4, Part12.MISO
  N181: J24.pin5, Part12.SCK
  N182: J24.pin6, Part12.GND#10
  N183: J24.pin7, Part12.ANA
  N184: J24.pin8, Part12.GND#8
  N185: J25.pin1, Part12.RESET
  N186: J25.pin2, Part12.DIO0
  N187: J25.pin3, Part12.DIO1
  N188: J25.pin4, Part12.DIO2
  N189: J25.pin5, Part12.DIO3
  N190: J25.pin6, Part12.DIO4
  N191: J25.pin7, Part12.DIO5
  N192: J25.pin8, Part12.3V3
